// Digital circuit 4-bit-adder.dig as structural Verilog
module _4_bit_adder (
  input  A_0,
  input  B_0,
  input  A_1,
  input  B_1,
  input  A_2,
  input  B_2,
  input  A_3,
  input  B_3,
  output S_0,
  output S_1,
  output S_2,
  output S_3
);

  wire full_adder_1_c_i_plus_1, full_adder_2_c_i_plus_1, full_adder_3_c_i_plus_1;

  full_adder full_adder_1 (.C_i(1'b0), .X(A_0), .Y(B_0), .S_i_plus_1(S_0), .C_i_plus_1(full_adder_1_c_i_plus_1));
  full_adder full_adder_2 (
    .C_i(full_adder_1_c_i_plus_1), .X(A_1), .Y(B_1), .S_i_plus_1(S_1), .C_i_plus_1(full_adder_2_c_i_plus_1));
  full_adder full_adder_3 (
    .C_i(full_adder_2_c_i_plus_1), .X(A_2), .Y(B_2), .S_i_plus_1(S_2), .C_i_plus_1(full_adder_3_c_i_plus_1));
  full_adder full_adder_4 (.C_i(full_adder_3_c_i_plus_1), .X(A_3), .Y(B_3), .S_i_plus_1(S_3));  // open: C_i_plus_1
endmodule
