// Digital circuit 4x3-memory.dig as structural Verilog
module _4x3_memory (
  input  A_1,
  input  A_0,
  input  D_0,
  input  D_1,
  input  D_2,
  input  WE,
  output D_2_2,
  output D_1_2,
  output D_0_2
);

  wire and_1_out, and_2_out, and_3_out, and_4_out, and_5_out, and_6_out, and_7_out, and_8_out, and_9_out,
       and_10_out, and_11_out, and_12_out, and_13_out, and_14_out, and_15_out, and_16_out, and_17_out,
       and_18_out, and_19_out, and_20_out, d_latch_1_q, d_latch_2_q, d_latch_3_q, d_latch_4_q, d_latch_5_q,
       d_latch_6_q, d_latch_7_q, d_latch_8_q, d_latch_9_q, d_latch_10_q, d_latch_11_q, d_latch_12_q;

  and and_1 (and_1_out, ~A_0, ~A_1);  // And
  and and_2 (and_2_out, A_0, ~A_1);  // And
  and and_3 (and_3_out, ~A_0, A_1);  // And
  and and_4 (and_4_out, A_0, A_1);
  and and_5 (and_5_out, and_1_out, WE);
  and and_6 (and_6_out, and_2_out, WE);
  and and_7 (and_7_out, and_3_out, WE);
  and and_8 (and_8_out, and_4_out, WE);
  d_latch d_latch_1 (.D(D_2), .WE(and_5_out), .Q(d_latch_1_q));
  d_latch d_latch_2 (.D(D_2), .WE(and_6_out), .Q(d_latch_2_q));
  d_latch d_latch_3 (.D(D_2), .WE(and_7_out), .Q(d_latch_3_q));
  d_latch d_latch_4 (.D(D_2), .WE(and_8_out), .Q(d_latch_4_q));
  and and_9 (and_9_out, and_1_out, d_latch_1_q);
  and and_10 (and_10_out, and_2_out, d_latch_2_q);
  and and_11 (and_11_out, and_3_out, d_latch_3_q);
  and and_12 (and_12_out, and_4_out, d_latch_4_q);
  or or_1 (D_2_2, and_9_out, and_10_out, and_11_out, and_12_out);
  d_latch d_latch_5 (.D(D_1), .WE(and_5_out), .Q(d_latch_5_q));
  d_latch d_latch_6 (.D(D_1), .WE(and_6_out), .Q(d_latch_6_q));
  d_latch d_latch_7 (.D(D_1), .WE(and_7_out), .Q(d_latch_7_q));
  d_latch d_latch_8 (.D(D_1), .WE(and_8_out), .Q(d_latch_8_q));
  and and_13 (and_13_out, and_1_out, d_latch_5_q);
  and and_14 (and_14_out, and_2_out, d_latch_6_q);
  and and_15 (and_15_out, and_3_out, d_latch_7_q);
  and and_16 (and_16_out, and_4_out, d_latch_8_q);
  or or_2 (D_1_2, and_13_out, and_14_out, and_15_out, and_16_out);
  d_latch d_latch_9 (.D(D_0), .WE(and_5_out), .Q(d_latch_9_q));
  d_latch d_latch_10 (.D(D_0), .WE(and_6_out), .Q(d_latch_10_q));
  d_latch d_latch_11 (.D(D_0), .WE(and_7_out), .Q(d_latch_11_q));
  d_latch d_latch_12 (.D(D_0), .WE(and_8_out), .Q(d_latch_12_q));
  and and_17 (and_17_out, and_1_out, d_latch_9_q);
  and and_18 (and_18_out, and_2_out, d_latch_10_q);
  and and_19 (and_19_out, and_3_out, d_latch_11_q);
  and and_20 (and_20_out, and_4_out, d_latch_12_q);
  or or_3 (D_0_2, and_17_out, and_18_out, and_19_out, and_20_out);
endmodule
