// Digital circuit 4x3-memory_2.dig as structural Verilog
module _4x3_memory_2 (
  input  A_1,
  input  A_0,
  input  D_0,
  input  D_1,
  input  D_2,
  input  WE,
  output D_2_2,
  output D_1_2,
  output D_0_2
);

  wire and_1_out, and_2_out, and_3_out, and_4_out, d_latch_1_q, d_latch_2_q, d_latch_3_q, d_latch_4_q,
       d_latch_5_q, d_latch_6_q, d_latch_7_q, d_latch_8_q, d_latch_9_q, d_latch_10_q, d_latch_11_q,
       d_latch_12_q, decoder_1_out_0, decoder_1_out_1, decoder_1_out_2, decoder_1_out_3;

  Decoder #(.Selector_Bits(2)) decoder_1 (
    .sel({A_1, A_0}), .out_0(decoder_1_out_0), .out_1(decoder_1_out_1), .out_2(decoder_1_out_2),
    .out_3(decoder_1_out_3));
  and and_1 (and_1_out, decoder_1_out_0, WE);
  and and_2 (and_2_out, decoder_1_out_1, WE);
  and and_3 (and_3_out, decoder_1_out_2, WE);
  and and_4 (and_4_out, decoder_1_out_3, WE);
  d_latch d_latch_1 (.D(D_2), .WE(and_1_out), .Q(d_latch_1_q));
  d_latch d_latch_2 (.D(D_2), .WE(and_2_out), .Q(d_latch_2_q));
  d_latch d_latch_3 (.D(D_2), .WE(and_3_out), .Q(d_latch_3_q));
  d_latch d_latch_4 (.D(D_2), .WE(and_4_out), .Q(d_latch_4_q));
  Multiplexer #(.Selector_Bits(2)) multiplexer_1 (
    .sel({A_1, A_0}), .in_0(d_latch_1_q), .in_1(d_latch_2_q), .in_2(d_latch_3_q), .in_3(d_latch_4_q),
    .out(D_2_2));
  d_latch d_latch_5 (.D(D_1), .WE(and_1_out), .Q(d_latch_5_q));
  d_latch d_latch_6 (.D(D_1), .WE(and_2_out), .Q(d_latch_6_q));
  d_latch d_latch_7 (.D(D_1), .WE(and_3_out), .Q(d_latch_7_q));
  d_latch d_latch_8 (.D(D_1), .WE(and_4_out), .Q(d_latch_8_q));
  Multiplexer #(.Selector_Bits(2)) multiplexer_2 (
    .sel({A_1, A_0}), .in_0(d_latch_5_q), .in_1(d_latch_6_q), .in_2(d_latch_7_q), .in_3(d_latch_8_q),
    .out(D_1_2));
  d_latch d_latch_9 (.D(D_0), .WE(and_1_out), .Q(d_latch_9_q));
  d_latch d_latch_10 (.D(D_0), .WE(and_2_out), .Q(d_latch_10_q));
  d_latch d_latch_11 (.D(D_0), .WE(and_3_out), .Q(d_latch_11_q));
  d_latch d_latch_12 (.D(D_0), .WE(and_4_out), .Q(d_latch_12_q));
  Multiplexer #(.Selector_Bits(2)) multiplexer_3 (
    .sel({A_1, A_0}), .in_0(d_latch_9_q), .in_1(d_latch_10_q), .in_2(d_latch_11_q), .in_3(d_latch_12_q),
    .out(D_0_2));
endmodule
