// Digital circuit 8bit-register.dig as structural Verilog
module _8bit_register (
  input  WE,
  input  [15:0] D_in,
  output [7:0] D_out
);

  d_latch d_latch_1 (.D(D_in[0]), .WE(WE), .Q(D_out[0]));
  d_latch d_latch_2 (.D(D_in[1]), .WE(WE), .Q(D_out[1]));
  d_latch d_latch_3 (.D(D_in[2]), .WE(WE), .Q(D_out[2]));
  d_latch d_latch_4 (.D(D_in[3]), .WE(WE), .Q(D_out[3]));
  d_latch d_latch_5 (.D(D_in[4]), .WE(WE), .Q(D_out[4]));
  d_latch d_latch_6 (.D(D_in[5]), .WE(WE), .Q(D_out[5]));
  d_latch d_latch_7 (.D(D_in[6]), .WE(WE), .Q(D_out[6]));
  d_latch d_latch_8 (.D(D_in[7]), .WE(WE), .Q(D_out[7]));
  // Pins of 8 and 16 bits meet at D_in
endmodule
