// Digital circuit alarm.dig as structural Verilog
module alarm (
  input  A,
  input  S,
  input  M,
  input  D
);

  wire and_1_out, and_2_out, and_3_out, or_1_out;

  and and_1 (and_1_out, ~A, S, D);  // And
  and and_2 (and_2_out, A, M);
  and and_3 (and_3_out, A, D);
  or or_1 (or_1_out, and_1_out, and_2_out, and_3_out);
  LED led_1 (.in(or_1_out));
endmodule
