// Digital circuit buffered-latch.dig as structural Verilog
module buffered_latch (
  input  D,
  input  clk,
  output Q
);

  wire nand_1_out, nand_2_out, nand_3_out, nand_4_out, nand_5_out, nand_6_out, nand_8_out, not_1_out;

  nand nand_1 (nand_1_out, D, not_1_out);
  nand nand_2 (nand_2_out, not_1_out, ~D);  // NAnd
  nand nand_3 (nand_3_out, nand_1_out, nand_4_out);
  nand nand_4 (nand_4_out, nand_3_out, nand_2_out);
  not not_1 (not_1_out, clk);
  // Probe on nand_3_out
  nand nand_5 (nand_5_out, nand_3_out, clk);
  nand nand_6 (nand_6_out, clk, ~nand_3_out);  // NAnd
  nand nand_7 (Q, nand_5_out, nand_8_out);
  nand nand_8 (nand_8_out, Q, nand_6_out);
  // Probe on Q
endmodule
