// Digital circuit d-latch-unstable.dig as structural Verilog
module d_latch_unstable (
  input  D,
  input  WE,
  output Q,
  output nQ
);

  wire nand_1_out, nand_2_out;

  nand nand_1 (nand_1_out, D, WE);
  nand nand_2 (nand_2_out, WE, ~D);  // NAnd
  nand nand_3 (Q, nand_1_out, nQ);
  nand nand_4 (nQ, Q, nand_2_out);
endmodule
