// Digital circuit d-latch.dig as structural Verilog
module d_latch (
  input  D,
  input  WE,
  output Q
);

  wire nand_1_out, nand_2_out, nand_4_out;

  nand nand_1 (nand_1_out, D, WE);
  nand nand_2 (nand_2_out, WE, ~D);  // NAnd
  nand nand_3 (Q, nand_1_out, nand_4_out);
  nand nand_4 (nand_4_out, Q, nand_2_out);
endmodule
