// Digital circuit decoder.dig as structural Verilog
module decoder (
  input  A,
  input  B
);

  wire and_1_out, and_2_out, and_3_out, and_4_out;

  and and_1 (and_1_out, ~A, ~B);  // And
  and and_2 (and_2_out, ~A, B);  // And
  and and_3 (and_3_out, A, ~B);  // And
  and and_4 (and_4_out, A, B);
  LED led_1 (.in(and_1_out));
  LED led_2 (.in(and_2_out));
  LED led_3 (.in(and_3_out));
  LED led_4 (.in(and_4_out));
endmodule
