// Digital circuit detour-mealy.dig as structural Verilog
module detour_mealy (
  input  S,
  input  C
);

  wire and_1_out, and_2_out, and_3_out, and_4_out, and_5_out, and_6_out, and_7_out, C_1, C_2, C_3, not_1_out,
       not_2_out, or_1_out, Z_0_n, Z_1_n;

  not not_1 (not_1_out, Z_1_n);
  not not_2 (not_2_out, Z_0_n);
  and and_1 (and_1_out, S, Z_0_n, not_1_out);
  and and_2 (and_2_out, S, not_2_out, Z_1_n);
  and and_3 (and_3_out, S, not_2_out);
  and and_4 (and_4_out, S, not_1_out);
  and and_5 (and_5_out, S, not_2_out);
  and and_6 (and_6_out, S, Z_0_n, not_1_out);
  and and_7 (and_7_out, S, not_2_out, Z_1_n);
  and and_8 (C_3, S, not_2_out, Z_1_n);
  or or_1 (or_1_out, and_1_out, and_2_out);
  or or_2 (C_1, and_4_out, and_5_out);
  or or_3 (C_2, and_6_out, and_7_out);
  D_FF u_Z_1_n (.D(or_1_out), .C(C), .Q(Z_1_n));  // open: nQ
  D_FF u_Z_0_n (.D(and_3_out), .C(C), .Q(Z_0_n));  // open: nQ
  LED led_1 (.in(C_1));
  LED led_2 (.in(C_1));
  // Probe detour.fsm on {Z_1_n, Z_0_n}
  LED led_3 (.in(C_2));
  LED led_4 (.in(C_2));
  LED led_5 (.in(C_3));
endmodule
