// Digital circuit detour.dig as structural Verilog
module detour (
  input  S,
  input  clk
);

  wire and_1_out, and_2_out, and_3_out, and_4_out, and_5_out, and_6_out, and_7_out, D0_q, D1_q, or_1_out,
       or_2_out;

  and and_1 (and_1_out, S, D0_q);
  and and_2 (and_2_out, S, D1_q);
  and and_3 (and_3_out, S, D1_q);
  and and_4 (and_4_out, S, D0_q, D1_q);
  and and_5 (and_5_out, ~D0_q, S);  // And
  and and_6 (and_6_out, ~D0_q, D1_q, S);  // And
  and and_7 (and_7_out, D0_q, ~D1_q, S);  // And
  or or_1 (or_1_out, and_1_out, and_2_out);
  or or_2 (or_2_out, and_6_out, and_7_out);
  LED led_1 (.in(or_1_out));
  LED led_2 (.in(or_1_out));
  D_FF D0 (.D(and_5_out), .C(clk), .Q(D0_q));  // open: nQ
  D_FF D1 (.D(or_2_out), .C(clk), .Q(D1_q));  // open: nQ
  LED led_3 (.in(and_3_out));
  LED led_4 (.in(and_3_out));
  LED led_5 (.in(and_4_out));

  // Notes on the sheet:
  //   Combinational Logic
  //   Sequential Logic
endmodule
