// Digital circuit down-counter.dig as structural Verilog
module down_counter (
  input  clk
);

  wire and_1_out, and_2_out, not_1_out, or_1_out, S_0, S_1;

  and and_1 (and_1_out, ~S_1, ~S_0);  // And
  and and_2 (and_2_out, S_1, S_0);
  or or_1 (or_1_out, and_1_out, and_2_out);
  D_FF u_S_1 (.D(or_1_out), .C(clk), .Q(S_1));  // open: nQ
  LED led_1 (.in(S_1));
  not not_1 (not_1_out, S_0);
  D_FF u_S_0 (.D(not_1_out), .C(clk), .Q(S_0));  // open: nQ
  LED led_2 (.in(S_0));

  // Notes on the sheet:
  //   S^n_1
  //   S_1
  //   S^n_0
  //   S_0
endmodule
