// Digital circuit full-adder.dig as structural Verilog
module full_adder (
  input  C_i,
  input  X,
  input  Y,
  output S_i_plus_1,
  output C_i_plus_1
);

  wire and_1_out, and_2_out, and_3_out, and_4_out, and_5_out, and_6_out, and_7_out;

  and and_1 (and_1_out, ~X, ~Y, C_i);  // And
  and and_2 (and_2_out, ~X, Y, ~C_i);  // And
  and and_3 (and_3_out, X, ~Y, ~C_i);  // And
  and and_4 (and_4_out, X, Y, C_i);
  and and_5 (and_5_out, X, Y);
  and and_6 (and_6_out, X, C_i);
  and and_7 (and_7_out, Y, C_i);
  or or_1 (S_i_plus_1, and_1_out, and_2_out, and_3_out, and_4_out);
  or or_2 (C_i_plus_1, and_5_out, and_6_out, and_7_out);
endmodule
