// Digital circuit mux-2X1.dig as structural Verilog
module mux_2X1 (
  input  A,
  input  B,
  input  S
);

  wire and_1_out, and_2_out, or_1_out;

  and and_1 (and_1_out, ~S, A);  // And
  or or_1 (or_1_out, and_2_out, and_1_out);
  LED led_1 (.in(or_1_out));
  and and_2 (and_2_out, S, B);
endmodule
