// Digital circuit mux-4x2.dig as structural Verilog
module mux_4x2 (
  input  A,
  input  B,
  input  C,
  input  D,
  input  S_0,
  input  S_1
);

  wire and_1_out, and_2_out, and_3_out, and_4_out, multiplexer_1_out, or_1_out;

  and and_1 (and_1_out, ~S_0, ~S_1, A);  // And
  and and_2 (and_2_out, S_0, ~S_1, B);  // And
  LED led_1 (.in(or_1_out));
  and and_3 (and_3_out, ~S_0, S_1, C);  // And
  or or_1 (or_1_out, and_4_out, and_3_out, and_2_out, and_1_out);
  and and_4 (and_4_out, S_0, S_1, D);
  Multiplexer #(.Selector_Bits(2)) multiplexer_1 (
    .sel({S_1, S_0}), .in_0(A), .in_1(B), .in_2(C), .in_3(D), .out(multiplexer_1_out));
  LED led_2 (.in(multiplexer_1_out));
endmodule
